// Logisim project ProgettoA.circ as structural Verilog: 3 circuits, main circuit CicuitoSequenziale
module CicuitoSequenziale (
  input  TB,
  input  TA,
  input  Enable_Flip_Flop,
  input  Reset,
  output s0
);

  wire clock_1_out, d_ff_1_q;

  Circuito_Combinatorio circuito_combinatorio_1 (.s0(d_ff_1_q), .TB(TB), .TA(TA), .out_4(s0));
  Clock clock_1 (.out(clock_1_out));
  D_Flip_Flop d_ff_1 (
    .clk(clock_1_out), .D(s0), .Q(d_ff_1_q), .en(Enable_Flip_Flop), .reset(Reset));  // open: Qn, preset

  // Notes on the sheet:
  //   Clock
endmodule

module Circuito_Combinatorio (
  input  s0,
  input  TB,
  input  TA,
  output out_4
);

  wire and_1_out, and_2_out, not_1_out, not_2_out;

  not not_1 (not_1_out, s0);
  not not_2 (not_2_out, TA);
  and and_1 (and_1_out, not_1_out, TB);
  and and_2 (and_2_out, s0, not_2_out);
  or or_1 (out_4, and_1_out, and_2_out);
endmodule

module semplificato (
  input  a,
  input  b,
  input  c,
  output x
);

  wire and_1_out, and_2_out, not_1_out, not_2_out;

  not not_1 (not_1_out, a);
  not not_2 (not_2_out, c);
  and and_1 (and_1_out, not_1_out, b);
  and and_2 (and_2_out, a, not_2_out);
  or or_1 (x, and_1_out, and_2_out);
endmodule
