// Logisim project ProgettoB.circ as structural Verilog: 3 circuits, main circuit Circuito Sequenziale
module Circuito_Sequenziale (
  input  in_1,
  input  TA,
  input  TB,
  input  Reset,
  output out_5,
  output out_6
);

  wire clock_1_out, combinatorio_1_s0___s1, combinatorio_1_s1_2;

  Clock clock_1 (.out(clock_1_out));
  Combinatorio combinatorio_1 (
    .s0(out_5), .s1(out_6), .TA(TA), .TB(TB), .s0___s1(combinatorio_1_s0___s1), .s1_2(combinatorio_1_s1_2));
  D_Flip_Flop d_ff_1 (
    .clk(clock_1_out), .D(combinatorio_1_s0___s1), .Q(out_5), .preset(Reset), .en(in_1));  // open: Qn, reset
  D_Flip_Flop d_ff_2 (
    .clk(clock_1_out), .D(combinatorio_1_s1_2), .Q(out_6), .preset(Reset), .en(in_1));  // open: Qn, reset

  // Notes on the sheet:
  //   Enable D FlipFlop
  //   Clock
endmodule

module Combinatorio (
  input  s0,
  input  s1,
  input  TA,
  input  TB,
  output s0___s1,
  output s1_2
);

  wire and_1_out, and_2_out, and_3_out, not_1_out, not_2_out;

  not not_1 (not_1_out, s0);
  not not_2 (not_2_out, TA);
  and and_1 (and_1_out, not_1_out, TB);
  and and_2 (and_2_out, not_1_out, s1);
  and and_3 (and_3_out, s1, not_2_out);
  or or_1 (s1_2, and_1_out, and_2_out, and_3_out);

  assign s0___s1 = s1;

  // Notes on the sheet:
  //   s0^ TB
  //   s0^ s1
  //   s1 TA^
  //   s1 = s0^ TB  + s0^ s1  + s1 TA
  //   s0
endmodule

module semplificato (
  input  a,
  input  b,
  input  c,
  input  d,
  output x,
  output y
);

  wire and_1_out, and_2_out, and_3_out, not_1_out, not_2_out, not_3_out;

  not not_1 (not_1_out, a);
  and and_1 (and_1_out, not_1_out, d);
  not not_2 (not_2_out, a);
  and and_2 (and_2_out, not_2_out, b);
  and and_3 (and_3_out, b, not_3_out);
  not not_3 (not_3_out, c);
  or or_1 (y, and_1_out, and_2_out, and_3_out);

  assign x = b;
endmodule
